# Fritzing sketch 1BasicLED (saved by Fritzing 0.9.9b)
breadboards: 1

parts:
  VCC1 = Battery
  LED1 = smd LED [color="Red (633nm)" package="0805 [SMD]"]

nets:
  N1: VCC1.-, LED1.cathode
  N2: VCC1.+, LED1.anode

notes:
  <= Long Side
