# Fritzing sketch 2LEDWResistor (saved by Fritzing 0.9.9b)
breadboards: 1

parts:
  VCC1 = Battery
  LED1 = smd LED [color="Red (633nm)" package="0805 [SMD]"]
  R1 = Resistor [tolerance=±5% resistance=220 package="2010 [SMD]"]

nets:
  N1: VCC1.-, R1.Pin_1
  N2: VCC1.+, LED1.anode
  N3: LED1.cathode, R1.Pin_0

notes:
  <= Long Side
  330 Ohm Resistor =>
