# Fritzing sketch 4LEDWButtonPowerPi (saved by Fritzing 0.9.9b)
breadboards: 1

parts:
  LED1 = smd LED [color="Red (633nm)" package="0805 [SMD]"]
  R1 = Resistor [tolerance=±5% resistance=220 package="2010 [SMD]"]
  S1 = Pushbutton [package="[THT]"]
  MCU1 = Raspberry Pi Zero

nets:
  N1: LED1.cathode, R1.Pin_0
  N2: LED1.anode, S1.Pin_3, S1.Pin_4
  N3: R1.Pin_1, MCU1.pin_6, MCU1.pin_9
  N4: S1.Pin_1, S1.Pin_2, MCU1.pin_2, MCU1.pin_4

notes:
  <= Long Side
  330 Ohm Resistor =>
