# Fritzing sketch 7SevenSegmentDisplay (saved by Fritzing 0.9.9b)
breadboards: 1

parts:
  LED1 = smd LED [color="Red (633nm)" package="0805 [SMD]"]
  R1 = Resistor [tolerance=±5% resistance=220 package="2010 [SMD]"]
  MCU1 = Raspberry Pi Zero
  S1 = Pushbutton [package="[THT]"]
  Part1 = 0.56" 7-segment LED Backpack [part_number=878]

nets:
  N1: LED1.cathode, R1.Pin_0
  N2: LED1.anode, MCU1.pin_8
  N3: R1.Pin_1, MCU1.pin_6, MCU1.pin_9, MCU1.pin_14, Part1.GND
  N4: MCU1.pin_2, MCU1.pin_4, S1.Pin_1, S1.Pin_2, Part1.VDD
  N5: MCU1.pin_3, Part1.SDA
  N6: MCU1.pin_5, Part1.SCL
  N7: MCU1.pin_10, S1.Pin_3, S1.Pin_4

notes:
  <= Long Side
  330 Ohm Resistor =>

custom parts:
  0.56" 7-segment LED Backpack: This 0.56" 7-segment LED display includes a driver chip for simple control via an I2C interface. The backpack features address-selection jumpers so you can connect up to eight displays on a single I2C bus.
