# Fritzing sketch PiZeroADC_PhotoResistor (saved by Fritzing 0.9.9b)
breadboards: 1

parts:
  MCU1 = Raspberry Pi Zero
  U1 = MCP3002 [package="DIP8 [THT]"]
  R1 = PHOTOCELL [package=photocell-kit]
  R2 = Resistor [package="2512 [SMD]"]

nets:
  N1: MCU1.pin_2, U1.Vin_(Voltage_in), R1.P$1
  N2: MCU1.pin_6, MCU1.pin_9, MCU1.pin_39, U1.Ground, R2.Pin_1
  N3: MCU1.pin_19, U1.DIn_(MOSI)
  N4: MCU1.pin_21, U1.DOut_(MISO)
  N5: MCU1.pin_23, U1.CLK_(Clock)
  N6: MCU1.pin_24, U1.ChipSelect
  N7: U1.CH0, R1.P$2, R2.Pin_0

notes:
  Photo Resistor
  10K Resistor

custom parts:
  MCP3002: The classic 555 general purpose timer/oscillator.
  Resistor: Resistor Basic schematic elements and footprints for 0603, 1206, and PTH resistors.
